# Fritzing sketch jellyfish (saved by Fritzing 0.9.2b)
breadboards: 2

parts:
  LED1 = smd LED [color="Blue (430nm)" package="1206 [SMD]"]
  LED3 = smd LED [color="Blue (430nm)" package="1206 [SMD]"]
  LED5 = smd LED [color="Blue (430nm)" package="1206 [SMD]"]
  LED6 = smd LED [color="Blue (430nm)" package="1206 [SMD]"]
  LED7 = smd LED [color="Blue (430nm)" package="1206 [SMD]"]
  LED2 = smd LED [color="Blue (430nm)" package="1206 [SMD]"]
  R1 = Resistor [tolerance=±5% resistance=150 package="0603 [SMD]"]
  R2 = Resistor [tolerance=±5% resistance=150 package="0603 [SMD]"]
  R3 = Resistor [tolerance=±5% resistance=330 package="1206 [SMD]"]
  R4 = Resistor [tolerance=±5% resistance=2.88k package="0603 [SMD]"]
  Q1 = TRANSISTOR_NPN [package=to-92]
  R5 = Resistor [tolerance=±5% resistance=575 package="1206 [SMD]"]
  U1 = Voltage Regulator [package=to220-adj]
  U2 = 555 Timer [package="SO8 [SMD]"]
  U3 = Voltage Regulator [package=to220-adj]
  R6 = Resistor [tolerance=±5% resistance=3.3k package="0603 [SMD]"]
  R7 = Resistor [tolerance=±5% resistance=560 package="1206 [SMD]"]
  R8 = Resistor [tolerance=±5% resistance=33k package="0603 [SMD]"]
  LED8 = smd LED [color="Red (635nm)" package="1206 [SMD]"]
  Q2 = TRANSISTOR_NPN [package=to-92]
  R9 = Resistor [tolerance=±5% resistance=150 package="0603 [SMD]"]
  C1 = Ceramic Capacitor [capacitance=100µF package="1206 [SMD, multilayer]"]
  LED9 = smd LED [color="Red (635nm)" package="1206 [SMD]"]
  R10 = Resistor [tolerance=±5% resistance=150 package="0603 [SMD]"]
  LED11 = smd LED [color="Red (635nm)" package="1206 [SMD]"]
  LED12 = smd LED [color="Red (635nm)" package="1206 [SMD]"]
  R11 = Resistor [tolerance=±5% resistance=180 package="0603 [SMD]"]
  C2 = Ceramic Capacitor [capacitance=100µF package="1206 [SMD, multilayer]"]
  C3 = Ceramic Capacitor [capacitance=100nF package="1206 [SMD, multilayer]"]
  C4 = Ceramic Capacitor [capacitance=10µF package="1206 [SMD, multilayer]"]
  R12 = Resistor [tolerance=±5% resistance=150 package="0603 [SMD]"]
  LED13 = smd LED [color="Red (635nm)" package="1206 [SMD]"]
  LED14 = smd LED [color="Red (635nm)" package="1206 [SMD]"]

nets (from the schematic view):
  N1: LED1.cathode, LED2.anode
  N2: LED1.anode, R1.Pin_1
  N3: LED3.cathode, LED7.cathode, Q1.C
  N4: LED3.anode, LED2.cathode
  N5: LED5.cathode, LED6.anode
  N6: LED5.anode, R2.Pin_1
  N7: LED6.cathode, LED7.anode
  N8: R1.Pin_0, R2.Pin_0, R3.Pin_1, U1.OUT
  N9: R3.Pin_0, R4.Pin_1, U1.ADJ
  GND: R4.Pin_0, Q1.E, U2.Pin_1, C1.1, LED9.cathode, LED12.cathode, R11.Pin_0, C2.1, C3.1, C4.1, LED14.cathode
  N10: Q1.B, R5.Pin_0
  N11: U2.Pin_2, U2.Pin_6, R8.Pin_1, Q2.B, C1.0
  N12: U2.Pin_3, R8.Pin_0
  N13: U2.Pin_4, U2.Pin_8, U3.OUT, R7.Pin_1, Q2.C, C3.0, C4.0
  N14: U3.ADJ, R6.Pin_0, R7.Pin_0
  N15: U3.IN, C2.0
  N16: R6.Pin_1, R11.Pin_1
  N17: LED8.cathode, LED9.anode
  N18: LED8.anode, R9.Pin_1
  N19: Q2.E, R9.Pin_0, R10.Pin_1
  N20: R10.Pin_0, LED11.anode
  N21: LED11.cathode, LED12.anode
  N22: R12.Pin_0, LED13.anode
  N23: LED13.cathode, LED14.anode

notes:
  Solid Blue LED Setup
  Fading RED LED Setup
  555 requires 9V.
