# Fritzing sketch tentacle control board (saved by Fritzing 0.9.2b)
circuit board: 7.66031cm x 3.19536cm
breadboards: 1

parts:
  IC1 = Voltage Regulator [package=to220-igo]
  R1 = Resistor [tolerance=±5% resistance=220 package="1206 [SMD]"]
  R2 = Resistor [tolerance=±5% resistance=220 package="1206 [SMD]"]
  R3 = Resistor [tolerance=±5% resistance=220 package="1206 [SMD]"]
  Q1 = TRANSISTOR_NPN [package=to-92]
  Q2 = TRANSISTOR_NPN [package=to-92]
  Q3 = TRANSISTOR_NPN [package=to-92]
  R4 = Resistor [tolerance=±5% resistance=220 package="1206 [SMD]"]
  R5 = Resistor [tolerance=±5% resistance=220 package="1206 [SMD]"]
  R6 = Resistor [tolerance=±5% resistance=220 package="1206 [SMD]"]
  R7 = Resistor [tolerance=±5% resistance=220 package="1206 [SMD]"]
  R8 = Resistor [tolerance=±5% resistance=220 package="1206 [SMD]"]
  R9 = Resistor [tolerance=±5% resistance=220 package="1206 [SMD]"]
  R10 = Resistor [tolerance=±5% resistance=220 package="1206 [SMD]"]
  R11 = Resistor [tolerance=±5% resistance=220 package="1206 [SMD]"]
  R12 = Resistor [tolerance=±5% resistance=220 package="1206 [SMD]"]
  R13 = Resistor [tolerance=±5% resistance=220 package="1206 [SMD]"]
  R14 = Resistor [tolerance=±5% resistance=220 package="1206 [SMD]"]
  R15 = Resistor [tolerance=±5% resistance=220 package="1206 [SMD]"]
  R16 = Resistor [tolerance=±5% resistance=220 package="1206 [SMD]"]
  R17 = Resistor [tolerance=±5% resistance=220 package="1206 [SMD]"]
  R18 = Resistor [tolerance=±5% resistance=220 package="1206 [SMD]"]
  R19 = Resistor [tolerance=±5% resistance=220 package="1206 [SMD]"]
  R20 = Resistor [tolerance=±5% resistance=220 package="1206 [SMD]"]
  R21 = Resistor [tolerance=±5% resistance=220 package="1206 [SMD]"]
  J1 = Power Jack [package=power_jack_slot]

nets:
  N1: IC1.GND, R2.Pin_1, R3.Pin_1
  N2: IC1.IN, J1.PWR
  N3: IC1.OUT, R3.Pin_0, R4.Pin_1, R8.Pin_1, R10.Pin_1, R14.Pin_1, R16.Pin_1, R20.Pin_1
  N4: R1.Pin_0, Q1.E, Q2.E, Q3.E, J1.GNDBREAK
  N5: R1.Pin_1, R2.Pin_0
  N6: Q1.B, R6.Pin_1
  N7: Q2.B, R12.Pin_1
  N8: Q3.B, R18.Pin_1
  N9: R4.Pin_0, R5.Pin_1
  N10: R6.Pin_0, R7.Pin_1
  N11: R8.Pin_0, R9.Pin_1
  N12: R10.Pin_0, R11.Pin_1
  N13: R12.Pin_0, R13.Pin_1
  N14: R14.Pin_0, R15.Pin_1
  N15: R16.Pin_0, R17.Pin_1
  N16: R18.Pin_0, R19.Pin_1
  N17: R20.Pin_0, R21.Pin_1

notes:
  kmkingsbury
  Jellyfish
  v1.0
  GPIO
  Blue
  Yellow
  Red
